# Fritzing sketch ESP8266_ProgrammerMode (saved by Fritzing 0.8.7b)
breadboards: 1

parts:
  U1 = ESP8266 WiFi Module [part_number=ESP8266]
  Part1 = Arduino Uno (Rev3)
  S1 = Momentary Switch [package=ksa_sealed_tac_switch]
  LED1 = LED - 5mm [color="Red (633nm)" package="5 mm [THT]"]

nets:
  N1: U1.RXD, Part1.D0/RX
  VCC: U1.VCC, U1.CH_PD, Part1.3V3
  GND: U1.GPIO_0, U1.GND, Part1.RESET, Part1.GND, S1.3, LED1.cathode
  N2: U1.RST, S1.1
  N3: U1.GPIO_2, LED1.anode
  N4: U1.TXD, Part1.D1/TX

notes:
  Placing ESP8266 in Programmer Mode
  Press the reset switch on bread board when arduino IDE is trying to connect to the Module
  To start code on ESP, remove wire from GPIO to GND and press reset button

custom parts:
  ESP8266 WiFi Module: Generic WiFi Module based on the ESP8266 with onboard PCB antenna and UART communications
